# Fritzing sketch Zigbee RFID (saved by Fritzing 1.0.2b)
circuit board: 8.7cm x 5.3cm
breadboards: 1

parts:
  Zigbee_Left = Zigbee-PA-Left [form="♀ (female)" package=THT]
  Zigbee_Right = Zigbee-PA-Right [form="♀ (female)" package=THT]
  Flash = Zigbee-SmartRF-Connector [form="♀ (female)" package=THT]
  PN532 = PN532-Header [form="♀ (female)" package=THT]
  Arduino = Arduino Nano Every
  Power = female pin header, 2 pins [form="♀ (female)"]
  LED = female pin header, 2 pins [form="♀ (female)"]
  Buzzer = female pin header, 2 pins [form="♀ (female)"]

nets:
  GND: Zigbee_Left.GND, Flash.GND, PN532.GND, Arduino.GND, Arduino.D13~, Power.pin1, LED.pin2, Buzzer.pin1
  N1: Zigbee_Left.P2.1, Flash.P2.1
  N2: Zigbee_Left.P2.2, Flash.P2.2
  N3: Zigbee_Right.RST, Flash.RST
  N4: Zigbee_Right.P0.2, Arduino.TX
  N5: Zigbee_Right.P0.4, Arduino.D2
  N6: Zigbee_Right.P0.6, Arduino.D3~
  N7: Zigbee_Right.P0.5, Arduino.D4
  VCC: Zigbee_Right.VCC, Flash.VCC, PN532.VCC, Arduino.VIN, Power.pin2
  N8: PN532.SDA, Arduino.A4
  N9: PN532.SCL, Arduino.A5
  N10: Arduino.D5~, Buzzer.pin2
  N11: Arduino.D6~, LED.pin1

custom parts:
  Zigbee-PA-Left: Generic double row female header
  Zigbee-PA-Right: Generic double row female header
  Zigbee-SmartRF-Connector: Generic double row female header
  PN532-Header: Generic female header
  Arduino Nano Every: The Nano Every is Arduino’s 5V compatible board in the smallest available form factor: 45x18mm! The Arduino Nano is the preferred board for many projects requiring a small and easy to use microcontroller board. The small footprint and low price, make the Nano Every particularly suited for wearable inventions, low cost robotics, electronic musical instruments, and general use to control smaller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
